// Logisim project IT012_Lab01_25520495.circ as structural Verilog
module Warmup (
  input  A,
  input  B,
  output F
);

  wire not_1_out;

  not not_1 (not_1_out, B);
  and and_1 (F, A, not_1_out);
endmodule

module TN1 (
  input  A,
  input  B,
  input  C,
  output NAND,
  output AND,
  output A_prime,
  output OR,
  output NOR,
  output XOR,
  output XNOR,
  output XOR3,
  output CHAIN,
  output NAND3
);

  wire nand_2_out;

  xnor xnor_1 (XNOR, A, B);
  nand nand_1 (NAND, A, B);
  not not_1 (A_prime, A);
  and and_1 (AND, A, B);
  or or_1 (OR, B, A);
  nor nor_1 (NOR, B, A);
  ExactlyOne xor_1 (.out(XOR3), .in0(A), .in1(B), .in2(C));
  nand nand_2 (nand_2_out, A, B);
  xor xor_2 (XOR, A, B);
  nand nand_3 (CHAIN, nand_2_out, C);
  nand nand_4 (NAND3, A, B, C);
endmodule

module TN2 (
  input  x,
  input  y,
  input  z,
  output EQ4,
  output EQ1,
  output EQ3,
  output EQ2,
  output EQ5
);

  wire and_1_out, and_2_out, and_3_out, and_4_out, nand_1_out, nor_1_out, not_1_out, not_2_out, or_1_out,
       or_2_out, or_3_out, or_4_out, or_5_out;

  not not_1 (not_1_out, x);
  and and_1 (and_1_out, not_1_out, not_2_out);
  not not_2 (not_2_out, y);
  nor nor_1 (nor_1_out, x, y);
  and and_2 (and_2_out, y, z);
  or or_1 (or_1_out, x, z);
  nand nand_1 (nand_1_out, x, y);
  or or_2 (or_2_out, x, y);
  and and_3 (and_3_out, y, not_1_out);
  xnor xnor_1 (EQ1, and_1_out, nor_1_out);
  or or_3 (or_3_out, x, y);
  or or_4 (or_4_out, x, and_3_out);
  or or_5 (or_5_out, x, and_2_out);
  and and_4 (and_4_out, or_3_out, or_1_out);
  xnor xnor_2 (EQ4, x, or_4_out);
  xnor xnor_3 (EQ2, and_1_out, nand_1_out);
  xnor xnor_4 (EQ3, or_5_out, and_4_out);
  xnor xnor_5 (EQ5, or_4_out, or_2_out);
endmodule

module TN3 (
  input  A,
  input  B,
  input  C,
  input  D,
  output F
);

  wire A_prime_B_prime_CD_out, A_prime_B_prime_CD_prime_out, A_prime_BC_prime_D_out, A_prime_BCD_out,
       AB_prime_CD_out, ABC_prime_D_out, not_1_out, not_2_out, not_3_out, not_4_out;

  not not_1 (not_1_out, A);
  not not_2 (not_2_out, B);
  not not_3 (not_3_out, C);
  not not_4 (not_4_out, D);
  and A_prime_B_prime_CD_prime (A_prime_B_prime_CD_prime_out, not_1_out, not_2_out, C, not_4_out);
  and A_prime_B_prime_CD (A_prime_B_prime_CD_out, not_1_out, not_2_out, C, D);
  and A_prime_BC_prime_D (A_prime_BC_prime_D_out, not_1_out, B, not_3_out, D);
  and A_prime_BCD (A_prime_BCD_out, not_1_out, B, C, D);
  and AB_prime_CD (AB_prime_CD_out, A, not_2_out, C, D);
  and ABC_prime_D (ABC_prime_D_out, A, B, not_3_out, D);
  or or_1 (F, A_prime_B_prime_CD_prime_out, A_prime_B_prime_CD_out, A_prime_BC_prime_D_out, A_prime_BCD_out, AB_prime_CD_out, ABC_prime_D_out);
endmodule

module TN4 (
  input  A,
  input  B,
  input  C,
  input  D,
  output F_can,
  output EQ1,
  output EQ2,
  output F_sop,
  output F_pos
);

  wire A_prime_B_prime_CD_out, A_prime_B_prime_CD_prime_out, A_prime_BC_prime_D_out, A_prime_BCD_out,
       AB_prime_CD_out, ABC_prime_D_out, and_1_out, and_2_out, and_3_out, and_4_out, not_1_out, not_2_out,
       not_3_out, not_4_out, or_1_out, or_2_out, or_3_out, or_4_out;

  not not_1 (not_1_out, A);
  not not_2 (not_2_out, B);
  not not_3 (not_3_out, C);
  not not_4 (not_4_out, D);
  and and_1 (and_1_out, not_1_out, not_2_out, C);
  and and_2 (and_2_out, B, not_3_out, D);
  and and_3 (and_3_out, not_2_out, C, D);
  and and_4 (and_4_out, not_1_out, B, D);
  or or_1 (or_1_out, B, C);
  or or_2 (or_2_out, not_2_out, D);
  or or_3 (or_3_out, not_1_out, D);
  or or_4 (or_4_out, not_1_out, not_2_out, not_3_out);
  and A_prime_B_prime_CD_prime (A_prime_B_prime_CD_prime_out, not_1_out, not_2_out, C, not_4_out);
  and A_prime_B_prime_CD (A_prime_B_prime_CD_out, not_1_out, not_2_out, C, D);
  and A_prime_BC_prime_D (A_prime_BC_prime_D_out, not_1_out, B, not_3_out, D);
  and A_prime_BCD (A_prime_BCD_out, not_1_out, B, C, D);
  and AB_prime_CD (AB_prime_CD_out, A, not_2_out, C, D);
  and ABC_prime_D (ABC_prime_D_out, A, B, not_3_out, D);
  or or_5 (F_sop, and_1_out, and_2_out, and_3_out, and_4_out);
  and and_5 (F_pos, or_1_out, or_2_out, or_3_out, or_4_out);
  or or_6 (F_can, A_prime_B_prime_CD_prime_out, A_prime_B_prime_CD_out, A_prime_BC_prime_D_out, A_prime_BCD_out, AB_prime_CD_out, ABC_prime_D_out);
  xnor xnor_1 (EQ1, F_can, F_sop);
  xnor xnor_2 (EQ2, F_can, F_pos);
endmodule

module TN5 (
  input  A,
  input  B,
  input  C,
  output F
);

  wire xor_1_out;

  xor xor_1 (xor_1_out, A, B);
  xor xor_2 (F, xor_1_out, C);
endmodule
